# Fritzing sketch Circuitry Diagram (saved by Fritzing 0.9.3b)
breadboards: 2

parts:
  Part1 = Arduino Mega 2560 (Rev3)
  U1 = L9110 H-bridge module [part_number="L9110 H-bridge"]
  U2 = L9110 H-bridge module [part_number="L9110 H-bridge"]
  U3 = L9110 H-bridge module [part_number="L9110 H-bridge"]
  U4 = L9110 H-bridge module [part_number="L9110 H-bridge"]
  M1 = Stepper Motor - Unipolar
  M2 = Stepper Motor - Unipolar
  M3 = Stepper Motor - Unipolar
  M4 = Stepper Motor - Unipolar
  LCD1 = LCD screen
  R1 = Resistor [tolerance=±5% resistance=10k package="0603 [SMD]"]
  S1 = Pushbutton [package="[THT]"]
  S2 = Pushbutton [package="[THT]"]
  S3 = Pushbutton [package="[THT]"]

nets:
  VCC: Part1.5V, U1.VCC, U2.VCC, U3.VCC, U4.VCC, LCD1.LED+
  GND: Part1.GND, U1.GND, U2.GND, U3.GND, U4.GND, LCD1.VSS, LCD1.LED-, S1.Pin_1, S1.Pin_2, S2.Pin_1, S2.Pin_2, S3.Pin_1, S3.Pin_2
  N1: Part1.D22, LCD1.RS
  N2: Part1.D23, U1.B-IA
  N3: Part1.D24, LCD1.E, LCD1.DB0
  N4: Part1.D25, U1.B-IB
  N5: Part1.D26, LCD1.DB4
  N6: Part1.D27, U1.A-IA
  N7: Part1.D28, LCD1.DB5
  N8: Part1.D29, U1.A-IB
  N9: Part1.D30, LCD1.DB6
  N10: Part1.D31, U2.B-IA
  N11: Part1.D32, LCD1.DB7
  N12: Part1.D33, U2.B-IB
  N13: Part1.D34, S3.Pin_3, S3.Pin_4
  N14: Part1.D35, U2.A-IA
  N15: Part1.D36, S1.Pin_3, S1.Pin_4
  N16: Part1.D37, U2.A-IB
  N17: Part1.D38, S2.Pin_3, S2.Pin_4
  N18: Part1.D39, U3.B-IA
  N19: Part1.D41, U3.B-IB
  N20: Part1.D43, U3.A-IA
  N21: Part1.D45, U3.A-IB
  N22: Part1.D47, U4.B-IA
  N23: Part1.D49, U4.B-IB
  N24: Part1.D51, U4.A-IA
  N25: Part1.D53, U4.A-IB
  N26: U1.MOTOR_A-A, M1.D
  N27: U1.MOTOR_A-B, M1.COMMON_2
  N28: U1.MOTOR_B-A, M1.COMMON_1
  N29: U1.MOTOR_B-B, M1.A
  N30: U2.MOTOR_A-A, M2.D
  N31: U2.MOTOR_A-B, M2.B, M2.COMMON_2
  N32: U2.MOTOR_B-A, M2.COMMON_1
  N33: U2.MOTOR_B-B, M2.A
  N34: U3.MOTOR_A-A, M3.D
  N35: U3.MOTOR_A-B, M3.COMMON_2
  N36: U3.MOTOR_B-A, M3.COMMON_1
  N37: U3.MOTOR_B-B, M3.A
  N38: U4.MOTOR_A-A, M4.D
  N39: U4.MOTOR_A-B, M4.B, M4.COMMON_2
  N40: U4.MOTOR_B-A, M4.COMMON_1, M4.C
  N41: U4.MOTOR_B-B, M4.A
  N42: LCD1.VDD, LCD1.V0, R1.Pin_1
  N43: LCD1.R/W, R1.Pin_0
